# Fritzing sketch lsls-fritzing (saved by Fritzing 0.9.3b)
breadboards: 1

parts:
  PART1 = SparkFun Photon RedBoard [part_number=DEV-13321]
  LED2 = LED - 5mm [color="Green (570nm)" package="5 mm [THT]"]
  R1 = Resistor [tolerance=±5% resistance=330 package="2512 [SMD]"]
  R2 = PHOTOCELL [package=photocell]
  R3 = Resistor [tolerance=±5% resistance=330 package="2512 [SMD]"]

nets:
  N1: PART1.A0, R2.P$2, R3.Pin_0
  N2: PART1.GND, R1.Pin_1, R3.Pin_1
  N3: PART1.D6, LED2.cathode
  N4: PART1.3.3V, R2.P$1
  N5: LED2.anode, R1.Pin_0

custom parts:
  SparkFun Photon RedBoard: SparkFun RedBoard for Photon has the P1 module in an Arduino Uno R3 footprint. Please visit: www.sparkfun.com/products/13321
